# Fritzing sketch ESP8266-ETH (saved by Fritzing 0.9.3b)

parts:
  U1 = NodeMCU V1.0
  Part1 = Arduino Ethernet Shield (Rev3)

nets:
  N1: U1.D1, U1.D5, U1.D6, U1.D7, U1.D8, U1.3V3, Part1.ICSP_MISO, Part1.ICSP_SCK, Part1.ICSP_MOSI, Part1.ETH_CS
  VIN: U1.Vin, Part1.5V
  GND: U1.GND, Part1.GND

custom parts:
  NodeMCU V1.0: ESP8266 based NodeMCU V1.0
